# Fritzing sketch wiring_schematic_pcb2 (saved by Fritzing 0.9.3b)
circuit board: 8.12301cm x 4.70753cm
breadboards: 1

parts:
  Raspberry_Pi_2 = Raspberry Pi 2
  DHT22 = Humidity and Temperature Sensor RHT03
  R1 = PHOTOCELL [package=photocell-kit]
  U1 = 4-Channel 5v Relay Shield [package=relay-4ch5v10a]
  Servo1 = Basic Servo
  LED1 = smd LED [color="Red (633nm)" package="1206 [SMD]"]  # not connected
  R3 = Resistor [tolerance=±5% resistance=220 package="2512 [SMD]"]
  J1 = male pin header, 6 pins [form="♂ (male)"]
  J2 = male pin header, 4 pins [form="♂ (male)"]
  J3 = male pin header, 8 pins [form="♂ (male)"]
  R2 = Resistor [tolerance=±0.5% resistance=10k package="2512 [SMD]"]
  IC1 = MCP3008 8-channel 10-bit ADC [part_number=MCP3008]
  LED2 = RGB LED (com. cathode, rgb) [package="5 mm [THT]"]  # not connected
  LED = male pin header, 4 pins [form="♂ (male)"]
  R4 = Resistor [tolerance=±5% resistance=330 package=THT]
  R5 = Resistor [tolerance=±5% resistance=330 package=THT]
  R6 = Resistor [tolerance=±5% resistance=220 package=THT]
  J4 = male pin header, 16 pins [form="♂ (male)"]

nets (from the schematic view):
  3V3: Raspberry_Pi_2.3v3, DHT22.Vcc, R3.Pin_1, J2.pin1, R2.Pin_1, IC1.V_REF, IC1.VDD, J4.pin12
  N1: Raspberry_Pi_2.GPIO10, IC1.D_IN, J4.pin8
  N2: Raspberry_Pi_2.GPIO9, IC1.D_OUT, J4.pin9
  N3: Raspberry_Pi_2.GPIO11, IC1.CLK, J4.pin10
  GND: Raspberry_Pi_2.GND, DHT22.GND_2, R1.P$2, U1.GND, J1.pin1, J2.pin4, IC1.DGND, IC1.AGND, J4.pin2, J4.pin13
  N4: Raspberry_Pi_2.GPIO8, IC1.CS, J4.pin11
  5V: Raspberry_Pi_2.5V, U1.VCC, J1.pin6, J4.pin1
  N5: DHT22.Data-signal, J2.pin2, R2.Pin_0, J4.pin3
  N6: R1.P$1, R3.Pin_0, J3.pin8, IC1.CH0
  N7: U1.IN1, J1.pin2, J4.pin4
  N8: U1.IN2, J1.pin3, J4.pin5
  N9: U1.K1-Off, Servo1.gnd
  N10: U1.K1-On, Servo1.vcc
  N11: U1.K2-In, U1.K2-Off, U1.K3-In, U1.K3-On, U1.K4-Off
  N12: J1.pin4, J4.pin6
  N13: J1.pin5, J4.pin7
  N14: J3.pin1, IC1.CH7
  N15: J3.pin2, IC1.CH6
  N16: J3.pin3, IC1.CH5
  N17: J3.pin4, IC1.CH4
  N18: J3.pin5, IC1.CH3
  N19: J3.pin6, IC1.CH2
  N20: J3.pin7, IC1.CH1
  N21: LED.pin1, R5.Pin_0
  N22: LED.pin3, R6.Pin_1
  N23: LED.pin4, R4.Pin_0
  N24: R4.Pin_1, J4.pin16
  N25: R5.Pin_1, J4.pin14
  N26: R6.Pin_0, J4.pin15

notes:
  GHP-Shield v1
  relayheader
  a/d channels
  DHT22

custom parts:
  4-Channel 5v Relay Shield: 4 Channel 5v Relay Shield w. 2x SPD-06VDC-SD-C
